# Fritzing sketch victron remote (saved by Fritzing 0.9.3b)
circuit board: 7.97641cm x 10.7626cm
breadboards: 1

parts:
  GX1_R = Screw terminal - 2 pins generic [package=THT]
  AUX_R = Screw terminal - 2 pins generic [package=THT]
  MPPT_R = Screw terminal - 2 pins generic [package=THT]
  GX2_R = Screw terminal - 2 pins generic [package=THT]
  Bat = Screw terminal - 2 pins generic [package=THT]
  K1 = Screw terminal - 2 pins generic [package=THT]
  R1 = Resistor [tolerance=±5% resistance=220 package=THT]
  R3 = Resistor [tolerance=±5% resistance=220 package=THT]
  R4 = Resistor [tolerance=±5% resistance=220 package=THT]
  R2 = Resistor [tolerance=±5% resistance=220 package=THT]
  temp = Screw terminal - 3 pins [package=THT]
  R5 = Resistor [tolerance=±5% resistance=220 package=THT]
  GX_in_1 = Screw terminal - 2 pins generic [package=THT]
  GX_in_2 = Screw terminal - 2 pins generic [package=THT]
  AUX_in_2 = Screw terminal - 2 pins generic [package=THT]
  AUX_in_1 = Screw terminal - 2 pins generic [package=THT]
  power = Screw terminal - 3 pins [package=THT]
  oled = mystery part, 4 pins [chip_label=?]
  i2c_hub = mystery part, 4 pins [chip_label=?]
  flame = Screw terminal - 4 pins [package=THT]
  smoke = Screw terminal - 3 pins [package=THT]
  U1 = LuaNode32 / ESP32 [part_number=ESP32S-PIN30]
  Multiplus = WeMos D1 Mini Relay Shield
  MPTT = WeMos D1 Mini Relay Shield
  Battery = WeMos D1 Mini Relay Shield
  relay4 = WeMos D1 Mini Relay Shield

nets:
  N1: GX1_R.pin1, AUX_R.pin1, MPPT_R.pin1, GX2_R.pin1, temp.pin1, R5.Pin_0, power.pin1, oled.pin2, i2c_hub.pin2, flame.pin4, smoke.pin3, U1.3V3
  N2: GX1_R.pin2, U1.D35
  N3: AUX_R.pin2, U1.D26
  N4: MPPT_R.pin2, U1.D32
  N5: GX2_R.pin2, U1.D34
  N6: Bat.pin1, K1.pin1, R3.Pin_1, R2.Pin_1, temp.pin3, GX_in_1.pin2, GX_in_2.pin2, AUX_in_2.pin2, AUX_in_1.pin2, power.pin3, oled.pin1, i2c_hub.pin1, flame.pin3, U1.GND, Multiplus.G, MPTT.G, Battery.G, relay4.G
  N7: Bat.pin2, R1.Pin_0
  N8: K1.pin2, R4.Pin_0
  N9: R1.Pin_1, R2.Pin_0, U1.D33
  N10: R3.Pin_0, R4.Pin_1, U1.D25
  N11: temp.pin2, R5.Pin_1, U1.D23
  N12: GX_in_1.pin1, U1.D4
  N13: GX_in_2.pin1, U1.RX2
  N14: AUX_in_2.pin1, U1.TX2
  N15: AUX_in_1.pin1, U1.D5
  5V: power.pin2, U1.Vin, Multiplus.5V, MPTT.5V, Battery.5V, relay4.5V
  N16: oled.pin3, i2c_hub.pin4, U1.D22
  N17: oled.pin4, i2c_hub.pin3, U1.D21
  N18: flame.pin2, U1.D19
  N19: smoke.pin2, U1.D18
  N20: U1.D27, Battery.D1
  N21: U1.D14, MPTT.D1
  N22: U1.D12, relay4.D1
  N23: U1.D13, Multiplus.D1

notes:
  victron remote control
  Meaudre
  Robotics
  Victron Remote

custom parts:
  Screw terminal - 2 pins generic: Screw terminal with 2 pins, size increased to match part.
  Screw terminal - 3 pins: Screw terminal with 3 pins (size increased to match part)
  Screw terminal - 4 pins: Screw terminal with 4 pins (size increased to match part)
  LuaNode32 / ESP32: New Image for LuaNode32 DOIT ESP32 DEVKIT V1. Base parts from LuaNode32 / ESP32 ESP32 based LuaNode32 by G.Noorlander DOIT Esp32 DevKit v1 (30 pins long, 11 pins width) by Werner Rothschopf (modified by vanepp Dec 2018)
